// Logisim project imm_gen.circ as structural Verilog: 1 circuit, main circuit imm_gen
module imm_gen (
  input  [31:0] inst,
  input  [2:0] ImmSel,
  output [31:0] imm
);

  wire [31:0] bit_extender_1_out;

  assign bit_extender_1_out = {{20{inst[31]}}, inst[31:20]};  // Bit_Extender bit_extender_1
  Multiplexer #(.enable("false"), .select(3), .width(32)) multiplexer_1 (
    .in0(bit_extender_1_out), .out(imm), .sel(ImmSel));  // open: in1, in2, in3, in4, in5, in6, in7

  // Other names for the same wires on the sheet: Imm_for_addi[11:0] = inst[31:20]; Ins24_20[4:0] = inst[24:20];
  //   Ins31_25[6:0] = inst[31:25]; Ins6_0[6:0] = inst[6:0]; Opcode[6:0] = inst[6:0]; Ins11_7[4:0] = inst[11:7];
  //   rd[4:0] = inst[11:7]; funct3[2:0] = inst[14:12]; Ins14_12[2:0] = inst[14:12]; Ins19_15[4:0] = inst[19:15];
  //   rs1[4:0] = inst[19:15]

  // Notes on the sheet:
  //   INPUTS to your circuit
  //   DON'T CHANGE THE LOCATIONS OF THE INPUTS AND OUTPUTS!
  //   OUTPUT from your circuit
endmodule
